// Logisim project fibbonachi.circ as structural Verilog: 1 circuit, main circuit main
module main (
);

  wire clock_1_out;
  wire [7:0] adder_1_out, register_1_q, register_2_q;

  Clock clock_1 (.out(clock_1_out));
  Register register_1 (.D(register_2_q), .clk(clock_1_out), .Q(register_1_q));  // open: en, clr
  Adder adder_1 (.a(register_2_q), .b(register_1_q), .out(adder_1_out));  // open: cin, cout
  Register register_2 (.D(adder_1_out), .clk(clock_1_out), .Q(register_2_q));  // open: en, clr
endmodule
